# Fritzing sketch atom (saved by Fritzing 0.9.3b)
breadboards: 1

parts:
  M1 = DC Motor
  M4 = DC Motor
  S1 = H-Bridge with L298N
  Parte1 = Arduino Nano (Rev3.0)
  Parte3 = HC-SR04
  J1 = Infrared Proximity Sensor [part_number="IR LEFT"]
  J2 = Infrared Proximity Sensor [part_number="IR RIGHT"]

nets:
  N1: M1.pin_1, S1.M2-02
  N2: M1.pin_2, S1.M2-01
  N3: M4.pin_1, S1.M1-01
  N4: M4.pin_2, S1.M1-02
  GND: S1.GND, Parte1.GND, Parte3.GND, J1.GND, J2.GND
  VCC: S1.5V, Parte1.VIN, Parte3.VCC, J1.Vcc, J2.Vcc
  N5: S1.ENA, Parte1.D10
  N6: S1.IN1, Parte1.D8
  N7: S1.IN2, Parte1.D7
  N8: S1.IN3, Parte1.D4
  N9: S1.IN4, Parte1.D2
  N10: S1.ENB, Parte1.D9
  N11: Parte1.D5, Parte3.Trig
  N12: Parte1.A3, Parte3.Echo

custom parts:
  H-Bridge with L298N: h-bridge
