# Fritzing sketch km-chassis (saved by Fritzing 0.9.3b)
breadboards: 1

parts:
  Componente1 = Arduino Uno (Rev3)
  L298N1 = L298N DC motor driver
  VCC1 = Battery block 9V
  M1 = DC Motor
  M2 = DC Motor
  J1 = Basic Servo
  hc-sr1 = hc-sr04
  ASR = Infrared Proximity Sensor
  ASL = Infrared Proximity Sensor
  Bocina = Piezo Speaker
  TL-Right = Infrared Proximity Sensor
  TL-Left = Infrared Proximity Sensor

nets:
  N1: Componente1.A0, hc-sr1.Trig
  N2: Componente1.A1, hc-sr1.Echo, ASL.Vout
  N3: Componente1.A2, TL-Right.Vout
  N4: Componente1.A3, TL-Left.Vout
  N5: Componente1.A4/SDA, ASR.Vout
  N6: Componente1.D8, L298N1.IN2
  N7: Componente1.D9_PWM, L298N1.IN1
  N8: Componente1.D10_PWM/SS, L298N1.ENA
  N9: Componente1.D11_PWM/MOSI, J1.pulse
  N10: Componente1.D12/MISO, Bocina.pin2
  GND: Componente1.GND, L298N1.GND, VCC1.-, J1.gnd, hc-sr1.GND, ASR.GND, ASL.GND, Bocina.pin1, TL-Right.GND, TL-Left.GND
  N11: Componente1.D5_PWM, L298N1.ENB
  N12: Componente1.D6_PWM, L298N1.IN4
  N13: Componente1.D7, L298N1.IN3
  VCC: Componente1.VIN, L298N1.12V, VCC1.+, TL-Right.Vcc, TL-Left.Vcc
  N14: L298N1.OUT1, M2.pin_2
  N15: L298N1.OUT2, M2.pin_1
  N16: L298N1.OUT3, M1.pin_1
  N17: L298N1.OUT4, M1.pin_2
  VCC_2: L298N1.5V, J1.vcc, hc-sr1.VCC, ASR.Vcc, ASL.Vcc

custom parts:
  L298N DC motor driver: 2x DC motor driver with 78M05 positive voltage regulator (7..35 V) L298N: max 46 V, 2 A Set 5 V Enable jumper to enable 5 V regultor (needed for the L298N) and +5 V output at screw terminal or supply external +5 V at screw terminal Set ENA and/or ENB to +5 V to enable motor permanently or supply ENA and/or ENB with PWM signal IN1 and IN2 set rotation directory for motor A (OUT1/OUT2) IN2 and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
