# Fritzing sketch coche5 (saved by Fritzing 0.9.0b)
breadboards: 1

parts:
  Parte1 = Arduino Nano (Rev3.0)
  S1 = H-Bridge with L298N
  M1 = DC Motor
  M2 = DC Motor
  VCC1 = Battery block 9V
  Central = HC-SR04
  Derecho = HC-SR04
  Izquierdo = HC-SR04

nets:
  GND: Parte1.GND, S1.GND, VCC1.-, Central.GND, Derecho.GND, Izquierdo.GND
  N1: Parte1.D6, Derecho.Trig
  N2: Parte1.D7, Derecho.Echo
  N3: Parte1.D8, Izquierdo.Echo
  N4: Parte1.D9, Izquierdo.Trig
  N5: Parte1.D11/MOSI, Central.Echo
  N6: Parte1.D12/MISO, Central.Trig
  VCC: Parte1.5V, S1.5V, Central.VCC, Derecho.VCC, Izquierdo.VCC
  N7: Parte1.A5, S1.IN1
  N8: Parte1.A4, S1.IN2
  N9: Parte1.A3, S1.IN3
  N10: Parte1.A2, S1.IN4
  N11: S1.12V, VCC1.+
  N12: S1.M1-01, M2.pin_2
  N13: S1.M1-02, M2.pin_1
  N14: S1.M2-01, M1.pin_1
  N15: S1.M2-02, M1.pin_2

custom parts:
  H-Bridge with L298N: h-bridge
