# Fritzing sketch spider (saved by Fritzing 0.9.3b)
breadboards: 1

parts:
  PCA9685_(0x40) = 16-Channel 12-bit PWM Servo Driver - I2C [part_number=815]
  PCA9685_(0xd41) = 16-Channel 12-bit PWM Servo Driver - I2C [part_number=815]
  Componente4 = VERTER 5V USB Buck-Boost
  BAT1 = Battery Holders [package=lipo-1100mAh]
  Componente5 = Arduino Nano (Rev3.0)
  C1 = Ceramic Capacitor [capacitance="100 nF" package="0603 [SMD, multilayer]"]
  R2 = Resistor [tolerance=±5% resistance=68k package="0805 [SMD]"]
  R1 = Resistor [tolerance=±5% resistance=68k package="0805 [SMD]"]
  LED1 = LED - 3mm [color="Green (555nm)" package="3 mm [THT]"]
  LED2 = LED - 3mm [color="Red (633nm)" package="3 mm [THT]"]
  R3 = Resistor [tolerance=±5% resistance=330 package="0402 [SMD]"]
  R4 = Resistor [tolerance=±5% resistance=330 package="0402 [SMD]"]
  GY1_(0x68) = GY-521 (MPU-6050) [form="♀ (female)" package=THT]
  Componente6 = IR Receiver Breakout [package=PCB]

nets:
  N1: PCA9685_(0x40).PWRIN, PCA9685_(0xd41).PWRIN, Componente4.5.0V
  GND: PCA9685_(0x40).GND, PCA9685_(0xd41).GND, Componente4.GND, BAT1.-, Componente5.GND, C1.0, R2.Pin_1, R1.Pin_0, R3.Pin_0, R4.Pin_0, GY1_(0x68).pin2, Componente6.GND
  N2: PCA9685_(0x40).5.0V, PCA9685_(0xd41).5.0V
  VCC: PCA9685_(0x40).VCC, PCA9685_(0xd41).VCC, Componente5.5V, GY1_(0x68).pin1, Componente6.VCC
  N3: PCA9685_(0x40).SDA, PCA9685_(0xd41).SDA, Componente5.A4, GY1_(0x68).pin4
  N4: PCA9685_(0x40).SCL, PCA9685_(0xd41).SCL, Componente5.A5, GY1_(0x68).pin3
  N5: PCA9685_(0x40).OE, PCA9685_(0xd41).OE
  VIN: Componente4.VIN, BAT1.+, Componente5.VIN, C1.1
  N6: Componente5.D2, GY1_(0x68).pin8
  N7: Componente5.D4, LED1.anode
  N8: Componente5.D7, LED2.anode
  N9: Componente5.D8, Componente6.OUT
  N10: Componente5.A0, R2.Pin_0, R1.Pin_1

custom parts:
  16-Channel 12-bit PWM Servo Driver - I2C: You want to make a cool robot, maybe a hexapod walker, or maybe just a piece of art with a lot of moving parts. Or maybe you want to drive a lot of LEDs with precise PWM output. Using only two pins, control 16 free-running PWM outputs! You can even chain up 62 breakouts to control up to 992 PWM outputs.
  VERTER 5V USB Buck-Boost: VERTER can take battery voltages from 3-12VDC and output a nice 5V DC, which makes it a perfect universal power supply for your portable project! Where Verter really shines is when you have a battery or power range that can fluctuate a lot, or you don't know what you'll end up using.
  GY-521 (MPU-6050): Placa GY-521 basada en conjunto de acelerómetro+giroscopios MPU-6050
