# Fritzing sketch tank01 (saved by Fritzing 0.9.0b)
breadboards: 1

parts:
  Parte1 = Arduino Nano (Rev3.0)
  S1 = H-Bridge with L298N
  M1 = DC Motor
  M2 = DC Motor
  BAT1 = Battery Holders [package=lipo-1100mAh]
  U1 = LIPO-1000mAh [package=lipo-1000]
  SERVO_2 = Basic Servo
  SERVO_1 = Basic Servo
  Parte2 = SRF05 Ultrasonic Rangefinder

nets:
  GND: Parte1.GND, S1.GND, U1.-, SERVO_2.gnd, SERVO_1.gnd, Parte2.GND
  N1: Parte1.D2, S1.IN2
  N2: Parte1.D3, Parte2.Trig
  N3: Parte1.D4, S1.IN1
  N4: Parte1.D5, S1.ENA
  N5: Parte1.D6, S1.ENB
  N6: Parte1.D7, S1.IN4
  N7: Parte1.D8, S1.IN3
  N8: Parte1.D9, SERVO_1.pulse
  N9: Parte1.D10, SERVO_2.pulse
  VCC: Parte1.VIN, S1.5V, SERVO_2.vcc, SERVO_1.vcc
  5V: Parte1.5V, Parte2.VCC
  N10: Parte1.A3, Parte2.Echo
  N11: S1.12V, BAT1.+
  N12: S1.M1-01, M2.pin_1
  N13: S1.M1-02, M2.pin_2
  N14: S1.M2-01, M1.pin_2
  N15: S1.M2-02, M1.pin_1
  N16: BAT1.-, U1.+

notes:
  Motor A
  Forward:
  Input 1: +5V
  Input 2: GND

custom parts:
  H-Bridge with L298N: h-bridge
