# Fritzing sketch tank02 (saved by Fritzing 0.9.0b)
circuit board: 11.1399cm x 7.53748cm
circuit board: 11.1399cm x 7.53748cm
breadboards: 1

parts:
  Parte1 = Arduino Nano (Rev3.0)
  S1 = H-Bridge with L298N
  M1 = DC Motor
  M2 = DC Motor
  BAT1 = Battery Holders [package=lipo-1100mAh]
  U1 = LIPO-1000mAh [package=lipo-1000]
  Parte2 = SRF05 Ultrasonic Rangefinder
  LED1 = LED - 5mm [color="Red (633nm)" package="5 mm [THT]"]
  R1 = Resistor [tolerance=±5% resistance=220 package=THT]
  LED2 = LED - 5mm [color="Red (633nm)" package="5 mm [THT]"]
  R2 = Resistor [tolerance=±5% resistance=220 package=THT]
  LED3 = LED - 5mm [color="Red (633nm)" package="5 mm [THT]"]
  R3 = Resistor [tolerance=±5% resistance=220 package=THT]
  J1 = Infrared Proximity Sensor
  J2 = Infrared Proximity Sensor

nets:
  GND: Parte1.GND, S1.GND, U1.-, Parte2.GND, LED1.cathode, LED2.cathode, LED3.cathode, J1.GND, J2.GND
  N1: Parte1.D2, S1.IN2
  N2: Parte1.D3, Parte2.Trig
  N3: Parte1.D4, S1.IN1
  N4: Parte1.D5, S1.ENA
  N5: Parte1.D6, S1.ENB
  N6: Parte1.D7, S1.IN4
  N7: Parte1.D8, S1.IN3
  N8: Parte1.D9, J1.Vout
  N9: Parte1.D10, J2.Vout
  VCC: Parte1.VIN, S1.5V, J1.Vcc, J2.Vcc
  5V: Parte1.5V, Parte2.VCC
  N10: Parte1.A6, R1.Pin_0
  N11: Parte1.A5, R2.Pin_0
  N12: Parte1.A4, R3.Pin_0
  N13: Parte1.A3, Parte2.Echo
  N14: S1.12V, BAT1.+
  N15: S1.M1-01, M2.pin_1
  N16: S1.M1-02, M2.pin_2
  N17: S1.M2-01, M1.pin_2
  N18: S1.M2-02, M1.pin_1
  N19: BAT1.-, U1.+
  N20: LED1.anode, R1.Pin_1
  N21: LED2.anode, R2.Pin_1
  N22: LED3.anode, R3.Pin_1

notes:
  Motor A
  Forward:
  Input 1: +5V
  Input 2: GND

custom parts:
  H-Bridge with L298N: h-bridge
