# Fritzing sketch wd4 (saved by Fritzing 0.9.0b)
breadboards: 1

parts:
  M1 = DC Motor
  M2 = DC Motor
  M4 = DC Motor
  S1 = H-Bridge with L298N
  M3 = DC Motor
  Parte1 = Arduino Nano (Rev3.0)
  Parte2 = HC-SR04
  Parte3 = HC-SR04
  Parte4 = HC-SR04
  R3 = Resistor [package="2010 [SMD]"]
  R4 = Resistor [package="2010 [SMD]"]

nets:
  N1: M1.pin_1, M2.pin_1, S1.M2-02
  N2: M1.pin_2, M2.pin_2, S1.M2-01
  N3: M4.pin_1, S1.M1-01, M3.pin_1
  N4: M4.pin_2, S1.M1-02, M3.pin_2
  N5: S1.12V, R3.Pin_0
  GND: S1.GND, Parte1.GND, Parte2.GND, Parte3.GND, Parte4.GND, R4.Pin_1
  VCC: S1.5V, Parte1.VIN, Parte2.VCC, Parte3.VCC, Parte4.VCC
  N6: Parte1.D3, Parte2.Trig
  N7: Parte1.D5, Parte3.Trig
  N8: Parte1.D6, Parte4.Trig
  N9: Parte1.A5, R3.Pin_1, R4.Pin_0
  N10: Parte1.A4, Parte2.Echo
  N11: Parte1.A3, Parte3.Echo
  N12: Parte1.A2, Parte4.Echo

custom parts:
  H-Bridge with L298N: h-bridge
  Resistor: Resistor Basic schematic elements and footprints for 0603, 1206, and PTH resistors.
